// Logisim project processeur_ARO2.circ as structural Verilog: 3 circuits, main circuit main
module main (
);

  wire clk, RESET_out, sysclk;
  wire [0:0] processeur_aro2_1_instr_addr_o;
  wire [14:0] processeur_aro2_1_instr_addr_o_2;
  wire [15:0] instr_mem_1_instr_o;

  Button RESET (.out(RESET_out));
  Clock #(.highDuration(4), .lowDuration(4)) u_clk (.out(clk));
  Clock u_sysclk (.out(sysclk));
  // Probe on processeur_aro2_1_instr_addr_o_2
  instr_mem instr_mem_1 (.addr_i(processeur_aro2_1_instr_addr_o_2), .instr_o(instr_mem_1_instr_o));
  // Probe on instr_mem_1_instr_o
  processeur_ARO2 processeur_aro2_1 (
    .instr_data_i(instr_mem_1_instr_o), .memory_rd_data_i({16{1'b0}}), .rst_i(RESET_out), .clk_i(clk),
    .instr_addr_o({processeur_aro2_1_instr_addr_o_2, processeur_aro2_1_instr_addr_o[0]}));  // open: memory_addr_o, memory_wr_data_o, memory_str_data_o, memory_ldr_data, memory_high_byte_o, memory_low_byte_o

  // Notes on the sheet:
  //   Attention, votre version de Logisim
  //   ne contient pas de tracker. Si vous
  //   enregistrez votre projet, toutes les
  //   informations du tracker seront
  //   définitivement effacées.
endmodule

module processeur_ARO2 (
  input  [15:0] instr_data_i,
  input  [15:0] memory_rd_data_i,
  input  rst_i,
  input  clk_i,
  output [15:0] instr_addr_o,
  output [14:0] memory_addr_o,
  output [15:0] memory_wr_data_o,
  output memory_str_data_o,
  output memory_ldr_data,
  output memory_high_byte_o,
  output memory_low_byte_o
);


  assign instr_addr_o = {16{1'b0}};
  assign memory_addr_o = {15{1'b0}};
  assign memory_high_byte_o = 1'b0;
  assign memory_ldr_data = 1'b0;
  assign memory_low_byte_o = 1'b0;
  assign memory_str_data_o = 1'b0;
  assign memory_wr_data_o = {16{1'b0}};

  // Other names for the same wires on the sheet: clk_s = clk_i; instr_data_s[15:0] = instr_data_i;
  //   memory_rd_data_s[15:0] = memory_rd_data_i; rst_s = rst_i

  // Notes on the sheet:
  //   Attention, votre version de Logisim
  //   ne contient pas de tracker. Si vous
  //   enregistrez votre projet, toutes les
  //   informations du tracker seront
  //   définitivement effacées.
  //   Intruction memory inputs
  //   Memory interface inputs
  //   Standard inputs
  //   Processeur simplifié pour le cours ARO2
  //   Instruction memory outputs
  //   Memory interface outputs
endmodule

module instr_mem (
  input  [14:0] addr_i,
  output [15:0] instr_o
);

  ROM #(.addrWidth(15), .dataWidth(16)) rom_1 (.addr(addr_i), .data(instr_o));

  // Notes on the sheet:
  //   Attention, votre version de Logisim
  //   ne contient pas de tracker. Si vous
  //   enregistrez votre projet, toutes les
  //   informations du tracker seront
  //   définitivement effacées.
endmodule
